# Fritzing sketch vegimeter2 (saved by Fritzing 0.8.3b)
circuit board: 15cm x 9cm
breadboards: 3

parts:
  XBEE = XBee
  LR_5_0V = SPX29302 [part_number=SPX29300T-L-5-0 package=q5-dd_spx29300]
  Propeller_I = Parallax Propeller D40 [package="DIP [THT]"]
  Heater_Relay = RELAY [package=relay-jzc]
  Pump_Relay = RELAY [package=relay-jzc]
  R1 = Resistor [tolerance=±5% resistance=10k package=THT]
  5_MHz_XTAL = CRYSTAL [package=hc49us]
  Water_A_Temp = Header 3 [package=screwterminal-3.5mm-3_lock.007s]
  Soil_A_Temp = Header 3 [package=screwterminal-3.5mm-3_lock.007s]
  Soil_B_Temp = Header 3 [package=screwterminal-3.5mm-3_lock.007s]
  Soil_C_Temp = Header 3 [package=screwterminal-3.5mm-3_lock.007s]
  Soil_D_Temp = Header 3 [package=screwterminal-3.5mm-3_lock.007s]
  Air_Temp = TEMPERATURE-SENSOR [part_number=DS18B20 package=to-92]
  R3 = Resistor [tolerance=±5% resistance=10k package=THT]
  R4 = Resistor [tolerance=±5% resistance=1k package=THT]
  R5 = Resistor [tolerance=±5% resistance=1k package=THT]
  R6 = Resistor [tolerance=±5% resistance=4.7k package=THT]
  R7 = Resistor [tolerance=±5% resistance=1k package=THT]
  R8 = Resistor [tolerance=±5% resistance=1k package=THT]
  R9 = Resistor [tolerance=±5% resistance=1k package=THT]
  R12 = Resistor [tolerance=±5% resistance=220 package=THT]
  R13 = Resistor [tolerance=±5% resistance=220 package=THT]
  R14 = Resistor [tolerance=±5% resistance=100 package=THT]
  C3_(4_7uF) = Capacitor [package=cap-pth-small2]
  0_1_uF = Capacitor [package=cap-pth-small2]
  C2_(10_nF) = Capacitor [package=cap-pth-small2]
  ULN2803A = ULN2803A [package=THT]
  Mini_USB = USB Connectors [package=usb-b-pth]
  EEPROM = 24LC256 [package=THT]
  NPN = NPN-Transistor [package="TO92 [THT]"]
  Water_B_Temp = Header 3 [package=screwterminal-3.5mm-3_lock.007s]
  R16 = Resistor [tolerance=±5% resistance=1k package=THT]
  Reset = SWITCH-MOMENTARY-2 [package=tactile_switch_smd]
  USB_RX = LED - 5mm [color="Red (633nm)" package="5 mm [THT]"]
  USB_TX = LED - 5mm [color="Red (633nm)" package="5 mm [THT]"]
  XBEE_In = LED - 5mm [color="Red (633nm)" package="5 mm [THT]"]
  XBEE_Out = LED - 5mm [color="Red (633nm)" package="5 mm [THT]"]
  R32 = Resistor [tolerance=±20% resistance=10k package=THT]
  R31 = Resistor [tolerance=±5% resistance=33k package=THT]
  C32_(10_uF) = Electrolytic Capacitor [capacitance=10µF package="100 mil [THT, electrolytic]"]
  C31_(4_7_uF) = Electrolytic Capacitor [capacitance=4.7mF package="100 mil [THT, electrolytic]"]
  LR_3_3V = Voltage Regulator [package=to220-adj]
  Pump = Header 3 [package=screwterminal-3.5mm-3_lock.007s]
  Heater = Header 3 [package=screwterminal-3.5mm-3_lock.007s]
  Primary = Header 3 [package=screwterminal-3.5mm-3_lock.007s]
  R33 = Resistor [tolerance=±5% resistance=1k package=THT]
  R34 = Resistor [tolerance=±20% resistance=4.7k package=THT]
  R35 = Resistor [tolerance=±20% resistance=10k package=THT]
  LED11 = LED - 5mm [color="Red (633nm)" package="5 mm [THT]"]
  R36 = Resistor [tolerance=±5% resistance=220 package=THT]
  FT232RL = USB UART [package=ssop28db]

nets:
  VCC: XBEE.VCC, Propeller_I.VDD, R1.Pin_1, Water_A_Temp.3, Soil_A_Temp.3, Soil_B_Temp.3, Soil_C_Temp.3, Soil_D_Temp.3, Air_Temp.VCC, R4.Pin_0, R5.Pin_0, R6.Pin_0, R7.Pin_0, R8.Pin_0, R9.Pin_0, EEPROM.+V, Water_B_Temp.3, R16.Pin_0, XBEE_In.cathode, XBEE_Out.cathode, LR_3_3V.OUT
  N1: XBEE.pin2, Propeller_I.P9, R12.Pin_1
  N2: XBEE.pin3, Propeller_I.P8, R13.Pin_1
  GND: XBEE.GND, LR_5_0V.GND, Propeller_I.VSS, Propeller_I.BOEn, Heater_Relay.MAIN, Pump_Relay.MAIN, Water_A_Temp.1, Soil_A_Temp.1, Soil_B_Temp.1, Soil_C_Temp.1, Soil_D_Temp.1, Air_Temp.GND, R3.Pin_1, C3_(4_7uF).2, 0_1_uF.1, ULN2803A.0V, Mini_USB.GND, EEPROM.A0, EEPROM.A1, EEPROM.A2, EEPROM.0V, EEPROM.WP_-_Write_Protect, NPN.E, Water_B_Temp.1, Reset.2, R32.Pin_1, C32_(10_uF).-, C31_(4_7_uF).-, LR_3_3V.ADJ, Primary.3, R35.Pin_0, LED11.cathode, FT232RL.GND7, FT232RL.GND18, FT232RL.TEST
  N3: LR_5_0V.ENABLE, LR_5_0V.VIN, C31_(4_7_uF).+, LR_3_3V.IN, Heater.3, Primary.1
  N4: LR_5_0V.VOUT, Heater_Relay.COIL2, Pump_Relay.COIL2, R14.Pin_1, C3_(4_7uF).1, ULN2803A.COM_-_Common, R31.Pin_1, Pump.3, FT232RL.VCCIO, FT232RL.VCC
  N5: LR_5_0V.ADJUST, R31.Pin_0, C32_(10_uF).+, R33.Pin_0
  N6: Propeller_I.P0, Air_Temp.ADJ, R6.Pin_1
  N7: Propeller_I.P1, Water_A_Temp.2, R7.Pin_1
  N8: Propeller_I.P2, Soil_A_Temp.2, R5.Pin_1
  N9: Propeller_I.P3, Soil_B_Temp.2, R8.Pin_1
  N10: Propeller_I.P4, Soil_C_Temp.2, R4.Pin_1
  N11: Propeller_I.P5, Soil_D_Temp.2, R9.Pin_1
  N12: Propeller_I.P6, ULN2803A.In_2, ULN2803A.In_3
  N13: Propeller_I.P7, ULN2803A.In_4, ULN2803A.In_5
  N14: Propeller_I.RESn, NPN.C, Reset.1
  N15: Propeller_I.P10, Water_B_Temp.2, R16.Pin_1
  N16: Propeller_I.P11, R36.Pin_1
  N17: Propeller_I.XI, 5_MHz_XTAL.2
  N18: Propeller_I.XO, 5_MHz_XTAL.1
  N19: Propeller_I.P28, EEPROM.SCL_-_I2C_Clock
  N20: Propeller_I.P29, R1.Pin_0, EEPROM.SDA_-_I2C_Data
  N21: Propeller_I.P30, FT232RL.RXD
  N22: Propeller_I.P31, FT232RL.TXD
  N23: Heater_Relay.NO, Heater.1
  N24: Heater_Relay.COIL1, ULN2803A.Out_3, ULN2803A.Out_2
  N25: Pump_Relay.NO, Pump.1
  N26: Pump_Relay.COIL1, ULN2803A.Out_5, ULN2803A.Out_4
  N27: R3.Pin_0, C2_(10_nF).2, NPN.B
  N28: R12.Pin_0, XBEE_Out.anode
  N29: R13.Pin_0, XBEE_In.anode
  N30: R14.Pin_0, USB_RX.cathode, USB_TX.cathode
  N31: 0_1_uF.2, FT232RL.3V3OUT
  N32: C2_(10_nF).1, FT232RL.DTR
  N33: Mini_USB.D+, FT232RL.USBDP
  N34: Mini_USB.D-, FT232RL.USBDM
  N35: Mini_USB.VBUS, R34.Pin_1
  N36: USB_RX.anode, FT232RL.RXLED
  N37: USB_TX.anode, FT232RL.TXLED
  N38: R32.Pin_0, R33.Pin_1
  N39: R34.Pin_0, R35.Pin_1, FT232RL.RESET
  N40: LED11.anode, R36.Pin_0

notes:
  Vegimeter 2
  Rev 2
  www.bionicbunny.org
